# Fritzing sketch disting-mk4-labels (saved by Fritzing 0.9.9b)

parts:
  U1 = NodeMCU V1.0
  Squix1 = OLED 0.96" 128x64 I2C SSD1306
  Squix2 = OLED 0.96" 128x64 I2C SSD1306
  Squix3 = OLED 0.96" 128x64 I2C SSD1306
  J1 = shrouded pin header, 16 pins [form="♂ (shrouded male)"]
  R1 = Resistor [tolerance=±5% resistance=10k package="0805 [SMD]"]
  R2 = Resistor [tolerance=±5% resistance=10k package="0805 [SMD]"]
  part = Rotary Encoder [package=THT]  # not connected
  part_2 = Rotary Encoder [package=THT]  # not connected
  RE1 = Rotary Encoder [package=THT]
  U3 = Header 1 [package=1x01_offset]  # not connected
  U4 = Header 1 [package=1x01_offset]  # not connected
  U5 = Header 1 [package=1x01_offset]  # not connected
  U6 = Header 1 [package=1x01_offset]  # not connected
  R3 = Resistor [tolerance=±5% resistance=220 package="0805 [SMD]"]
  R4 = Resistor [tolerance=±5% resistance=220 package="0805 [SMD]"]

nets:
  N1: U1.D1, Squix1.SCL, Squix2.SCL, Squix3.SCL
  N2: U1.D2, Squix1.SCA
  N3: U1.D3, Squix2.SCA
  N4: U1.D4, Squix3.SCA
  VCC: U1.3V3, Squix1.VCC, Squix2.VCC, Squix3.VCC, R2.Pin_1, R4.Pin_0
  GND: U1.GND, Squix1.GND, Squix2.GND, Squix3.GND, J1.pin3, RE1.EncoderPinB, RE1.SwitchPinE
  N5: U1.D5, R1.Pin_0, RE1.EncoderPinA
  N6: U1.D6, R2.Pin_0, RE1.EncoderPinC
  N7: U1.D7, RE1.SwitchrPinD
  N8: U1.TX, R3.Pin_0
  N9: U1.Vin, J1.pin11

notes:
  Opto-isolator Circuit
  Fairchild 6n137 fast opto-coupler, 10Mbits/s rated
  Reverse protection diode is shottky with 30V or higher rating (1N5818 is 30V peak, 1A part)
  Input capacitor C1 should be 30V rated or higher
  Input LED forward voltage ~1.4V typ at 10mA forward current
  1MHz noise cutoff using input RC Low Pass filter, with 0.4us rise time
  Input current limit resistor is two 0.25W 3.3k resistors in parallel
  1.65k delivers
  ~9mA from 15V,
  ~15mA max at rated input voltage
  ~3.7mA at low input of 7V
  max power 300mW in input resistors at max voltage
  Larger input resistor can be used at expense of raising low end input voltage limit for reliable operation
  High level output current max 20uA results in 20mV offset
  Input threshold approx 2.5mA with 1k load resistor
  Designed for inputs of between 7V and 24V, 12-15V nominal
  Ve is for strobing the output and can be left NC if not used as has internal pullup
  Output resistor allows for full output low voltage at >5mA output current
  0.1uF Vcc decoupling required close to Vcc and GND pins
  For connection to Raspberry Pi use a level converter to convert from 5V logic to 3.3V.
  Input 7V to 24V, 15V nominal, 500kHz
  Note that grounds are not joined between source and circuit.
  Example use:
  DCC decoder front end isolator feeding Arduino
  This work by hobbyistdave is licensed under a Creative Commons Attribution-ShareAlike 4.0 International License
  No warranty either express or implied is given.
  This schematic was created with Fritzing.
  Inspired by Geoff Bunza at
  http://model-railroad-hobbyist.com/node/19446

custom parts:
  NodeMCU V1.0: ESP8266 based NodeMCU
  Rotary Encoder: Rotary Encoder from ALPSec11e with switch.
